// Logisim project cpu.circ as structural Verilog
module main (
  input  reset,
  output [31:0] instr,
  output RegWrite,
  output [4:0] RegAddr,
  output [31:0] RegData,
  output MemWrite,
  output [4:0] MemAddr,
  output [31:0] MemData
);

  wire AluSrc, beq, clk, eq, j_jal, jal, jr, not_1_out, RegDst, SignExt;
  wire [1:0] WhichtoReg;
  wire [2:0] AluOp;
  wire [4:0] multiplexer_1_out;
  wire [31:0] imm32, MemRead, multiplexer_3_out, multiplexer_5_out, PC_4, RegRead1, res;

  // Probe on instr[15:11]
  // Probe on instr[20:16]
  Clock clock_1 (.out(clk));
  IFU ifu_1 (
    .reset(reset), .clk(clk), .beq(beq), .eq(eq), .imm32(imm32), .instr(instr), .PC_jr(RegRead1),
    .j_jal(j_jal), .jr(jr), .PC_4(PC_4));
  // Probe on instr[25:21]
  // Probe on instr[20:16]
  Multiplexer #(.width(5), .enable("false")) multiplexer_1 (
    .in0(instr[15:11]), .in1(instr[20:16]), .out(multiplexer_1_out), .sel(RegDst));
  Multiplexer #(.width(5), .enable("false")) multiplexer_2 (
    .in0(multiplexer_1_out), .in1({5{1'b1}}), .out(RegAddr), .sel(jal));
  Multiplexer #(.select(2), .width(32), .enable("false")) multiplexer_3 (
    .in0({res[31:7], MemAddr, res[1:0]}), .in1(MemRead), .in2({instr[15:0], {16{1'b0}}}),
    .out(multiplexer_3_out), .sel(WhichtoReg));  // open: in3
  // Probe on WhichtoReg
  // Probe on RegAddr
  // Probe on RegData
  Multiplexer #(.width(32), .enable("false")) multiplexer_4 (
    .in0(multiplexer_3_out), .in1(PC_4), .out(RegData), .sel(jal));
  // Probe on nothing
  GRF grf_1 (
    .A1(instr[25:21]), .A2(instr[20:16]), .A3(RegAddr), .WD(RegData), .RD1(RegRead1), .RD2(MemData),
    .clk(clk), .reset(reset), .WE(not_1_out));
  // Probe on instr
  // Probe on instr
  not not_1 (not_1_out, RegWrite);
  EXT ext_1 (.imm16(instr[15:0]), .sign(SignExt), .imm32(imm32));
  // Probe on imm32
  // Probe on imm32
  // Probe on RegRead1
  // Probe on RegRead1
  Multiplexer #(.width(32), .enable("false")) multiplexer_5 (
    .in0(MemData), .in1(imm32), .out(multiplexer_5_out), .sel(AluSrc));
  Controller controller_1 (
    .op(instr[31:26]), .func(instr[5:0]), .AluOp(AluOp), .WeGrf(RegWrite), .WeDm(MemWrite), .beq(beq),
    .AluSrc(AluSrc), .WhichtoReg(WhichtoReg), .RegDst(RegDst), .SignExt(SignExt), .j_jal(j_jal), .jr(jr),
    .jal(jal));
  ALU alu_1 (.A(RegRead1), .B(multiplexer_5_out), .ALUop(AluOp), .eq(eq), .res({res[31:7], MemAddr, res[1:0]}));
  // Probe on AluOp
  // Probe on {res[31:7], MemAddr, res[1:0]}
  // Probe on {res[31:7], MemAddr, res[1:0]}
  // Probe on instr
  // Probe on RegAddr
  DM dm_1 (.clk(clk), .reset(reset), .A(MemAddr), .WD(MemData), .RD(MemRead), .WE(MemWrite));

  // Other names for the same wires on the sheet: func[5:0] = instr[5:0]; imm16[15:0] = instr[15:0];
  //   shamt[4:0] = instr[10:6]; Rd[4:0] = instr[15:11]; Rt[4:0] = instr[20:16]; Rs[4:0] = instr[25:21];
  //   op[5:0] = instr[31:26]; Mem[31:0] = MemData; RegRead2[31:0] = MemData; res[6:2] = MemAddr; WeDm = MemWrite;
  //   WeGrf = RegWrite

  // Notes on the sheet:
  //   CPU
  //   addu subu ori lw sw lui beq
  //   000+
  //   001-
  //   010&
  //   011|
endmodule

module GRF (
  input  clk,
  input  reset,
  input  WE,
  input  [4:0] A1,
  input  [4:0] A2,
  input  [4:0] A3,
  input  [31:0] WD,
  output [31:0] RD1,
  output [31:0] RD2
);

  wire [31:0] in00, in01, in02, in03, in04, in05, in06, in07, in08, in09, in10, in11, in12, in13, in14, in15,
       in16, in17, in18, in19, in20, in21, in22, in23, in24, in25, in26, in27, in28, in29, in30, in31, out00,
       out01, out02, out03, out04, out05, out06, out07, out08, out09, out10, out11, out12, out13, out14,
       out15, out16, out17, out18, out19, out20, out21, out22, out23, out24, out25, out26, out27, out28,
       out29, out30, out31;

  // Probe on WD
  Demultiplexer #(.select(5), .width(32), .tristate("true"), .enable("false")) demultiplexer_1 (
    .out0(in00), .out1(in01), .out2(in02), .out3(in03), .out4(in04), .out5(in05), .out6(in06), .out7(in07),
    .out8(in08), .out9(in09), .out10(in10), .out11(in11), .out12(in12), .out13(in13), .out14(in14),
    .out15(in15), .out16(in16), .out17(in17), .out18(in18), .out19(in19), .out20(in20), .out21(in21),
    .out22(in22), .out23(in23), .out24(in24), .out25(in25), .out26(in26), .out27(in27), .out28(in28),
    .out29(in29), .out30(in30), .out31(in31), .in(WD), .sel(A3));
  // Probe on A3
  Register #(.width(32)) register_1 (.D(in00), .Q(out00), .clr(1'b1));  // open: en, clk
  Register #(.width(32)) register_2 (.D(in08), .en(WE), .Q(out08), .clk(clk), .clr(reset));
  Register #(.width(32)) register_3 (.D(in16), .en(WE), .Q(out16), .clk(clk), .clr(reset));
  Register #(.width(32)) register_4 (.D(in24), .en(WE), .Q(out24), .clk(clk), .clr(reset));
  Register #(.width(32)) register_5 (.D(in01), .en(WE), .Q(out01), .clk(clk), .clr(reset));
  Register #(.width(32)) register_6 (.D(in09), .en(WE), .Q(out09), .clk(clk), .clr(reset));
  Register #(.width(32)) register_7 (.D(in17), .en(WE), .Q(out17), .clk(clk), .clr(reset));
  Register #(.width(32)) register_8 (.D(in25), .en(WE), .Q(out25), .clk(clk), .clr(reset));
  Multiplexer #(.select(5), .width(32), .enable("false")) multiplexer_1 (
    .in0(out00), .in1(out01), .in2(out02), .in3(out03), .in4(out04), .in5(out05), .in6(out06), .in7(out07),
    .in8(out08), .in9(out09), .in10(out10), .in11(out11), .in12(out12), .in13(out13), .in14(out14),
    .in15(out15), .in16(out16), .in17(out17), .in18(out18), .in19(out19), .in20(out20), .in21(out21),
    .in22(out22), .in23(out23), .in24(out24), .in25(out25), .in26(out26), .in27(out27), .in28(out28),
    .in29(out29), .in30(out30), .in31(out31), .out(RD1), .sel(A1));
  Register #(.width(32)) register_9 (.D(in02), .en(WE), .Q(out02), .clk(clk), .clr(reset));
  Register #(.width(32)) register_10 (.D(in10), .en(WE), .Q(out10), .clk(clk), .clr(reset));
  Register #(.width(32)) register_11 (.D(in18), .en(WE), .Q(out18), .clk(clk), .clr(reset));
  Register #(.width(32)) register_12 (.D(in26), .en(WE), .Q(out26), .clk(clk), .clr(reset));
  Register #(.width(32)) register_13 (.D(in03), .en(WE), .Q(out03), .clk(clk), .clr(reset));
  Register #(.width(32)) register_14 (.D(in11), .en(WE), .Q(out11), .clk(clk), .clr(reset));
  Register #(.width(32)) register_15 (.D(in19), .en(WE), .Q(out19), .clk(clk), .clr(reset));
  Register #(.width(32)) register_16 (.D(in27), .en(WE), .Q(out27), .clk(clk), .clr(reset));
  Register #(.width(32)) register_17 (.D(in04), .en(WE), .Q(out04), .clk(clk), .clr(reset));
  Register #(.width(32)) register_18 (.D(in12), .en(WE), .Q(out12), .clk(clk), .clr(reset));
  Register #(.width(32)) register_19 (.D(in20), .en(WE), .Q(out20), .clk(clk), .clr(reset));
  Register #(.width(32)) register_20 (.D(in28), .en(WE), .Q(out28), .clk(clk), .clr(reset));
  Multiplexer #(.select(5), .width(32), .enable("false")) multiplexer_2 (
    .in0(out00), .in1(out01), .in2(out02), .in3(out03), .in4(out04), .in5(out05), .in6(out06), .in7(out07),
    .in8(out08), .in9(out09), .in10(out10), .in11(out11), .in12(out12), .in13(out13), .in14(out14),
    .in15(out15), .in16(out16), .in17(out17), .in18(out18), .in19(out19), .in20(out20), .in21(out21),
    .in22(out22), .in23(out23), .in24(out24), .in25(out25), .in26(out26), .in27(out27), .in28(out28),
    .in29(out29), .in30(out30), .in31(out31), .out(RD2), .sel(A2));
  Register #(.width(32)) register_21 (.D(in05), .en(WE), .Q(out05), .clk(clk), .clr(reset));
  Register #(.width(32)) register_22 (.D(in13), .en(WE), .Q(out13), .clk(clk), .clr(reset));
  Register #(.width(32)) register_23 (.D(in21), .en(WE), .Q(out21), .clk(clk), .clr(reset));
  Register #(.width(32)) register_24 (.D(in29), .en(WE), .Q(out29), .clk(clk), .clr(reset));
  Register #(.width(32)) register_25 (.D(in06), .en(WE), .Q(out06), .clk(clk), .clr(reset));
  Register #(.width(32)) register_26 (.D(in14), .en(WE), .Q(out14), .clk(clk), .clr(reset));
  Register #(.width(32)) register_27 (.D(in22), .en(WE), .Q(out22), .clk(clk), .clr(reset));
  Register #(.width(32)) register_28 (.D(in30), .en(WE), .Q(out30), .clk(clk), .clr(reset));
  Register #(.width(32)) register_29 (.D(in07), .en(WE), .Q(out07), .clk(clk), .clr(reset));
  Register #(.width(32)) register_30 (.D(in15), .en(WE), .Q(out15), .clk(clk), .clr(reset));
  Register #(.width(32)) register_31 (.D(in23), .en(WE), .Q(out23), .clk(clk), .clr(reset));
  Register #(.width(32)) register_32 (.D(in31), .en(WE), .Q(out31), .clk(clk), .clr(reset));

  // Notes on the sheet:
  //   Global Register File
endmodule

module IFU (
  input  reset,
  input  clk,
  input  beq,
  input  eq,
  input  j_jal,
  input  jr,
  input  [31:0] imm32,
  input  [31:0] PC_jr,
  output [31:0] PC_4,
  output [31:0] instr
);

  wire and_1_out;
  wire [31:0] adder_1_out, multiplexer_1_out, multiplexer_2_out, NPC, PC, shifter_1_out;

  Shifter #(.width(32)) shifter_1 (.in(imm32), .\dist (5'b00010), .out(shifter_1_out));
  // Probe on shifter_1_out
  Adder #(.width(32)) adder_1 (.a(PC_4), .b(shifter_1_out), .out(adder_1_out));  // open: cin, cout
  // Probe on NPC[6:2]
  Register #(.width(32)) u_PC (.D(NPC), .Q(PC), .clk(clk), .clr(reset));  // open: en
  // Probe on PC_4
  Adder #(.width(32)) adder_2 (.a(PC), .b(32'h4), .out(PC_4));  // open: cin, cout
  // Probe on {PC[31:28], instr[25:0], 2'b00}
  Multiplexer #(.width(32), .enable("false")) multiplexer_1 (
    .in0(PC_4), .in1(adder_1_out), .out(multiplexer_1_out), .sel(and_1_out));
  and and_1 (and_1_out, beq, eq);
  // Probe on PC
  Multiplexer #(.width(32), .enable("false")) multiplexer_2 (
    .in0(multiplexer_1_out), .in1({PC[31:28], instr[25:0], 2'b00}), .out(multiplexer_2_out), .sel(j_jal));
  // Probe on PC[6:2]
  // Probe on PC[6:2]
  Multiplexer #(.width(32), .enable("false")) multiplexer_3 (.in0(multiplexer_2_out), .in1(PC_jr), .out(NPC), .sel(jr));
  ROM #(.addrWidth(5), .dataWidth(32)) rom_1 (.addr(PC[6:2]), .data(instr));  // open: sel
  // Probe on instr

  // Other names for the same wires on the sheet: PC_j_jal[31:2] = {PC[31:28], instr[25:0]}

  // Notes on the sheet:
  //   Instuction Fetch Unit
  //   contents of rom_1 (hex, n*v repeats v):
  //   3c000001 3c010001 3c020001 3c030001 3c040001 3c050001 3c060001 3c070001 3c080001 3c090001 3c0a0001
  //   3c0b0001 3c0c0001 3c0d0001 3c0e0001 3c0f0001 3c100001 3c110001 3c120001 3c130001 3c140001 3c150001
  //   3c160001 3c170001 3c180001 3c190001 3c1a0001 3c1b0001 3c1c0001 3c1d0001 3c1e0001 3c1f0001
endmodule

module ALU (
  input  [31:0] A,
  input  [31:0] B,
  input  [2:0] ALUop,
  output eq,
  output [31:0] res
);

  wire [31:0] adder_1_out, and_1_out, or_1_out, subtractor_1_out;

  Adder #(.width(32)) adder_1 (.a(A), .b(B), .out(adder_1_out));  // open: cin, cout
  Subtractor #(.width(32)) subtractor_1 (.a(A), .b(B), .out(subtractor_1_out));  // open: bin, bout
  assign and_1_out = A & B;  // AND_Gate and_1, 32 bits wide
  assign or_1_out = A | B;  // OR_Gate or_1, 32 bits wide
  // Probe on or_1_out
  // Probe on A
  // Probe on B
  Comparator #(.width(32)) comparator_1 (.a(B), .b(A), .eq(eq));  // open: gt, lt
  // Probe on res
  Multiplexer #(.select(3), .width(32), .enable("false")) multiplexer_1 (
    .in0(adder_1_out), .in1(subtractor_1_out), .in2(and_1_out), .in3(or_1_out), .out(res), .sel(ALUop));  // open: in4, in5, in6, in7

  // Notes on the sheet:
  //   Arithmetic and Logic Unit
  //   000+
  //   001-
  //   010&
  //   011|
endmodule

module EXT (
  input  [15:0] imm16,
  input  sign,
  output [31:0] imm32
);

  wire [31:0] bit_extender_1_out, bit_extender_2_out;

  assign bit_extender_1_out = {{16{1'b0}}, imm16};  // Bit_Extender bit_extender_1
  assign bit_extender_2_out = {{16{imm16[15]}}, imm16};  // Bit_Extender bit_extender_2
  Multiplexer #(.width(32), .enable("false")) multiplexer_1 (
    .in0(bit_extender_1_out), .in1(bit_extender_2_out), .out(imm32), .sel(sign));
endmodule

module DM (
  input  clk,
  input  reset,
  input  WE,
  input  [4:0] A,
  input  [31:0] WD,
  output [31:0] RD
);

  RAM #(.addrWidth(5), .dataWidth(32), .bus("separate")) ram_1 (
    .addr(A), .din(WD), .data(RD), .str(WE), .clk(clk), .clr(reset));  // open: sel, ld

  // Notes on the sheet:
  //   but mips address by byte(8 bits)
  //   Data Memory
  //   addressing by word(32 bits)
endmodule

module Controller (
  input  [5:0] op,
  input  [5:0] func,
  output [2:0] AluOp,
  output WeGrf,
  output WeDm,
  output beq,
  output AluSrc,
  output [1:0] WhichtoReg,
  output RegDst,
  output SignExt,
  output j_jal,
  output jal,
  output jr
);

  wire addu, j, lui, lw, not_1_out, not_2_out, not_3_out, not_4_out, not_5_out, not_6_out, not_7_out,
       not_8_out, not_9_out, not_10_out, not_11_out, not_12_out, ori, R, subu;

  // Probe on op
  not not_1 (not_1_out, op[5]);
  not not_2 (not_2_out, op[3]);
  not not_3 (not_3_out, op[4]);
  not not_4 (not_4_out, op[2]);
  not not_5 (not_5_out, op[1]);
  not not_6 (not_6_out, op[0]);
  // Probe on func
  not not_7 (not_7_out, func[5]);
  not not_8 (not_8_out, func[3]);
  not not_9 (not_9_out, func[2]);
  not not_10 (not_10_out, func[4]);
  not not_11 (not_11_out, func[0]);
  not not_12 (not_12_out, func[1]);
  and u_R (R, not_6_out, not_5_out, not_4_out, not_2_out, not_3_out, not_1_out);
  and u_addu (addu, R, func[0], not_12_out, not_9_out, not_8_out, not_10_out, func[5]);
  and u_subu (subu, R, func[0], func[1], not_9_out, not_8_out, not_10_out, func[5]);
  and u_ori (ori, op[0], not_5_out, op[2], op[3], not_3_out, not_1_out);
  and u_lw (lw, op[0], op[1], not_4_out, not_2_out, not_3_out, op[5]);
  and sw (WeDm, op[0], op[1], not_4_out, op[3], not_3_out, op[5]);
  and u_beq (beq, not_6_out, not_5_out, op[2], not_2_out, not_3_out, not_1_out);
  and u_lui (lui, op[0], op[1], op[2], op[3], not_3_out, not_1_out);
  and u_j (j, not_6_out, op[1], not_4_out, not_2_out, not_3_out, not_1_out);
  and u_jal (jal, op[0], op[1], not_4_out, not_2_out, not_3_out, not_1_out);
  and u_jr (jr, R, not_11_out, not_12_out, not_9_out, func[3], not_10_out, not_7_out);
  or or_1 (AluOp[0], subu, ori, 1'b0, 1'b0);
  buf or_2 (AluOp[1], ori);  // OR_Gate
  buf or_3 (AluOp[2], 1'b0);  // OR_Gate
  or or_4 (WhichtoReg[0], jal, lw);
  or or_5 (WhichtoReg[1], jal, lui);
  // Probe on AluOp
  or or_6 (WeGrf, addu, subu, lw, ori, lui, jal);
  or or_7 (AluSrc, ori, lw, WeDm, 1'b0);
  not not_13 (RegDst, R);
  or or_8 (SignExt, lw, WeDm, beq);
  or or_9 (j_jal, j, jal);

  // Other names for the same wires on the sheet: sw = WeDm

  // Notes on the sheet:
  //   Controller
  //   addu
  //   lw
  //   sw
  //   subu
  //   andi
  //   ori
  //   000+
  //   001-
  //   010&
  //   011|
  //   addu subu lw sw lui ori beq j jal jr
  //   01 Mem->Reg
  //   0 Rd is the WriteAddr
  //   0: reg, 1: ext(imm)
  //   00 AluRes->Reg
  //   10 lui to Reg
  //   11 PC+4 -> Reg
  //   1 Rt is the WriteAddr
endmodule

module simplified_main (
  input  reset
);

  wire AluSrc, beq, clk, eq, RegDst, SignExt, WeDm, WeGrf;
  wire [1:0] WhichtoReg;
  wire [2:0] AluOp;
  wire [4:0] MemAddr, RegAddr;
  wire [5:0] func;
  wire [15:6] imm16;
  wire [31:0] imm32, Mem, MemRead, multiplexer_3_out, RegData, RegRead1, res;
  wire [31:16] instr;

  // Probe on instr[25:21]
  // Probe on instr[20:16]
  // Probe on imm16[15:11]
  // Probe on instr[20:16]
  Clock clock_1 (.out(clk));
  // Probe on RegAddr
  Multiplexer #(.width(5), .enable("false")) multiplexer_1 (
    .in0(imm16[15:11]), .in1(instr[20:16]), .out(RegAddr), .sel(RegDst));
  Multiplexer #(.select(2), .width(32), .enable("false")) multiplexer_2 (
    .in0({res[31:7], MemAddr, res[1:0]}), .in1(MemRead), .in2({imm16, func, {16{1'b0}}}), .out(RegData),
    .sel(WhichtoReg));  // open: in3
  IFU ifu_1 (
    .reset(reset), .clk(clk), .beq(beq), .eq(eq), .imm32(imm32), .instr({instr, imm16, func}));  // open: PC_jr, j_jal, jr, PC_4
  // Probe on WhichtoReg
  GRF grf_1 (
    .A1(instr[25:21]), .A2(instr[20:16]), .A3(RegAddr), .WD(RegData), .RD1(RegRead1), .RD2(Mem), .clk(clk),
    .reset(reset), .WE(WeGrf));
  // Probe on nothing
  EXT ext_1 (.imm16({imm16, func}), .sign(SignExt), .imm32(imm32));
  Multiplexer #(.width(32), .enable("false")) multiplexer_3 (
    .in0(Mem), .in1(imm32), .out(multiplexer_3_out), .sel(AluSrc));
  ALU alu_1 (.A(RegRead1), .B(multiplexer_3_out), .ALUop(AluOp), .eq(eq), .res({res[31:7], MemAddr, res[1:0]}));
  Controller controller_1 (
    .op(instr[31:26]), .func(func), .AluOp(AluOp), .WeGrf(WeGrf), .WeDm(WeDm), .beq(beq), .AluSrc(AluSrc),
    .WhichtoReg(WhichtoReg), .RegDst(RegDst), .SignExt(SignExt));  // open: j_jal, jr, jal
  DM dm_1 (.clk(clk), .reset(reset), .A(MemAddr), .WD(Mem), .RD(MemRead), .WE(WeDm));

  // Other names for the same wires on the sheet: imm16[5:0] = func; instr[15:0] = {imm16, func};
  //   shamt[4:0] = imm16[10:6]; Rd[4:0] = imm16[15:11]; Rt[4:0] = instr[20:16]; Rs[4:0] = instr[25:21];
  //   op[5:0] = instr[31:26]; MemData[31:0] = Mem; RegRead2[31:0] = Mem; res[6:2] = MemAddr

  // Notes on the sheet:
  //   CPU
  //   000+
  //   001-
  //   010&
  //   011|
  //   addu subu ori lw sw lui beq
endmodule

module \IFU_同步_0x0003_0000  (
  input  reset,
  input  clk,
  input  beq,
  input  eq,
  input  [31:0] imm32,
  output [31:0] instr
);

  wire and_1_out, undriven;
  wire [31:0] adder_1_out, multiplexer_1_out, NPC, PC, PC_4, shifter_1_out;

  // Probe on NPC[6:2]
  Multiplexer #(.width(32), .enable("false")) multiplexer_1 (
    .in0(NPC), .in1(32'h3000), .out(multiplexer_1_out), .sel(reset));
  Register #(.width(32)) u_PC (.D(multiplexer_1_out), .Q(PC), .clk(clk), .clr(undriven));  // open: en
  Shifter #(.width(32)) shifter_1 (.in(imm32), .\dist (5'b00010), .out(shifter_1_out));
  // Probe on shifter_1_out
  // Probe on PC[6:2]
  Adder #(.width(32)) adder_1 (.a(PC_4), .b(shifter_1_out), .out(adder_1_out));  // open: cin, cout
  Adder #(.width(32)) adder_2 (.a(PC), .b(32'h4), .out(PC_4));  // open: cin, cout
  and and_1 (and_1_out, beq, eq);
  Multiplexer #(.width(32), .enable("false")) multiplexer_2 (.in0(PC_4), .in1(adder_1_out), .out(NPC), .sel(and_1_out));
  ROM #(.addrWidth(5), .dataWidth(32)) rom_1 (.addr(PC[6:2]), .data(instr));  // open: sel
  // Probe on instr

  // Notes on the sheet:
  //   Instuction Fetch Unit
  //   synchronous reset to 0x0000_3000
  //   contents of rom_1 (hex, n*v repeats v):
  //   34490064 344a00fa 344b00c8 12b6021 18a6823 ac4d0004 8c4e0004 3c0f0064 11a9fffe 11cdfffd
endmodule

module \IFU_异步_0x0000_3000  (
  input  reset,
  input  clk,
  input  beq,
  input  eq,
  input  [31:0] imm32,
  output [31:0] instr
);

  wire and_1_out, comparator_1_eq;
  wire [31:0] adder_2_out, NPC, PC, PC_4, PC_q, shifter_1_out;

  // Probe on NPC[6:2]
  Register #(.width(32)) u_PC (.D(NPC), .Q(PC_q), .clk(clk), .clr(reset));  // open: en
  Shifter #(.width(32)) shifter_1 (.in(imm32), .\dist (5'b00010), .out(shifter_1_out));
  // Probe on shifter_1_out
  Adder #(.width(32)) adder_1 (.a(PC), .b(32'h4), .out(PC_4));  // open: cin, cout
  Adder #(.width(32)) adder_2 (.a(PC_4), .b(shifter_1_out), .out(adder_2_out));  // open: cin, cout
  Comparator #(.width(32), .mode("unsigned")) comparator_1 (
    .a(PC_q), .b({32{1'b0}}), .eq(comparator_1_eq));  // open: gt, lt
  Multiplexer #(.width(32), .enable("false")) multiplexer_1 (.in0(PC_4), .in1(adder_2_out), .out(NPC), .sel(and_1_out));
  and and_1 (and_1_out, beq, eq);
  Multiplexer #(.width(32), .enable("false")) multiplexer_2 (
    .in0(PC_q), .in1(32'h3000), .out(PC), .sel(comparator_1_eq));
  // Probe on PC
  // Probe on PC[6:2]
  ROM #(.addrWidth(5), .dataWidth(32)) rom_1 (.addr(PC[6:2]), .data(instr));  // open: sel
  // Probe on instr

  // Notes on the sheet:
  //   Instuction Fetch Unit
  //   asynchronous reset to 0x0000_3000
  //   real PC
  //   contents of rom_1 (hex, n*v repeats v):
  //   34490064 344a00fa 344b00c8 12b6021 18a6823 ac4d0004 8c4e0004 3c0f0064 11a9fffe 11cdfffd
endmodule

module \IFU_异步_j  (
  input  reset,
  input  clk,
  input  beq,
  input  eq,
  input  j_jal,
  input  jr,
  input  [31:0] imm32,
  input  [31:0] PC_jr,
  output [31:0] PC_4,
  output [31:0] instr
);

  wire and_1_out, comparator_1_eq;
  wire [31:0] adder_1_out, multiplexer_1_out, multiplexer_3_out, NPC, PC, PC_q, shifter_1_out;

  Shifter #(.width(32)) shifter_1 (.in(imm32), .\dist (5'b00010), .out(shifter_1_out));
  // Probe on shifter_1_out
  // Probe on NPC[6:2]
  Adder #(.width(32)) adder_1 (.a(PC_4), .b(shifter_1_out), .out(adder_1_out));  // open: cin, cout
  Register #(.width(32)) u_PC (.D(NPC), .Q(PC_q), .clk(clk), .clr(reset));  // open: en
  Comparator #(.width(32), .mode("unsigned")) comparator_1 (
    .a(PC_q), .b({32{1'b0}}), .eq(comparator_1_eq));  // open: gt, lt
  // Probe on PC_4
  Adder #(.width(32)) adder_2 (.a(PC), .b(32'h4), .out(PC_4));  // open: cin, cout
  // Probe on {PC[31:28], instr[25:0], 2'b00}
  Multiplexer #(.width(32), .enable("false")) multiplexer_1 (
    .in0(PC_4), .in1(adder_1_out), .out(multiplexer_1_out), .sel(and_1_out));
  and and_1 (and_1_out, beq, eq);
  Multiplexer #(.width(32), .enable("false")) multiplexer_2 (
    .in0(PC_q), .in1(32'h3000), .out(PC), .sel(comparator_1_eq));
  Multiplexer #(.width(32), .enable("false")) multiplexer_3 (
    .in0(multiplexer_1_out), .in1({PC[31:28], instr[25:0], 2'b00}), .out(multiplexer_3_out), .sel(j_jal));
  // Probe on PC[6:2]
  Multiplexer #(.width(32), .enable("false")) multiplexer_4 (.in0(multiplexer_3_out), .in1(PC_jr), .out(NPC), .sel(jr));
  ROM #(.addrWidth(5), .dataWidth(32)) rom_1 (.addr(PC[6:2]), .data(instr));  // open: sel
  // Probe on instr

  // Other names for the same wires on the sheet: PC_j_jal[31:2] = {PC[31:28], instr[25:0]}

  // Notes on the sheet:
  //   Instuction Fetch Unit
  //   contents of rom_1 (hex, n*v repeats v):
  //   34100007 34110007 c000c05 3411000f 8000c09 12110001 3412000f 34140001 3e00008 2329821
endmodule
